// Logisim project datapath.circ as structural Verilog
module DataPath (
);

  wire [15:0] PC_q, ProgramROM_data, undriven;

  Register #(.width(16)) PC (.D(undriven), .Q(PC_q));  // open: en, clk, clr
  D_Flip_Flop d_ff_1 ();  // open: D, clk, Q, Qn, preset, reset
  ROM #(.addrWidth(16), .dataWidth(16)) ProgramROM (.addr(PC_q), .data(ProgramROM_data));
  Register #(.width(16)) InstructionRegister (.D(ProgramROM_data));  // open: en, clk, Q, clr
  RegisterFile registerfile_1 ();  // open: i_Clk, i_Rst, i_SelX, i_SelY, i_WriteEnable, i_WriteData, o_DataX, o_DataY
  Register ResultRegister ();  // open: D, en, clk, Q, clr
endmodule

// VHDL entity RegisterFile, as the project stores it:
library ieee;
use ieee.std_logic_1164.all;
use ieee.numeric_std_unsigned.all;

entity RegisterFile is
    port (
        i_Clk : in std_logic;
        i_Rst : in std_logic;
        i_SelX : in std_logic_vector(3 downto 0);
        i_SelY : in std_logic_vector(3 downto 0);
        i_WriteEnable : in std_logic;
        i_WriteData : in std_logic_vector(7 downto 0);
        o_DataX : out std_logic_vector(7 downto 0);
        o_DataY : out std_logic_vector(7 downto 0)
    );
end RegisterFile;

architecture RTL of RegisterFile is

    signal r_Registers: reg_arr_t;

begin

    process(i_Clk, i_Rst) is
    begin
        if rising_edge(i_Clk) then
            if i_Rst = '1' then
                r_Registers <= (others => (others => '0'));
            elsif i_WriteEnable = '1'
                then r_Registers(to_integer(i_SelX)) <= i_WriteData;
            end if;
        end if;
    end process;

    o_DataX <= r_Registers(to_integer(i_SelX));
    o_DataY <= r_Registers(to_integer(i_SelY));

end architecture;

// VHDL entity InstructionDecoder, as the project stores it:
library ieee;
use ieee.std_logic_1164.all;
use ieee.numeric_std.all;
use work.chip8_const_pkg.all;
use work.chip8_types_pkg.all;

entity InstructionDecoder is
    port(
        i_Clk : in std_logic;
        i_Rst : in std_logic;
        i_InstrOpcode : in chip8_instr_opcode_t;
        o_PCWrite : out std_logic;
        o_IRWrite : out std_logic;
        o_RRWrite : out std_logic;
        o_RegFileWrite : out std_logic;
        o_ALUOp : out chip8_alu_op_t
    );
end InstructionDecoder;

architecture RTL of InstructionDecoder is

    signal r_CurrState : chip8_fsm_state_t;

begin

    process(i_Clk, i_Rst) is
    begin
        if (i_Rst) then
            r_CurrState <= chip8_fsm_state_fetch;
        elsif rising_edge(i_Clk) then
            case r_CurrState is
                when chip8_fsm_state_fetch =>
                    r_CurrState <= chip8_fsm_state_decode;
                when chip8_fsm_state_decode =>
                    case i_InstrOpcode is
                        when chip8_instr_opcode_store_imm =>
                            r_CurrState <= chip8_fsm_state_writeVX;
                        when others =>
                            r_CurrState <= chip8_fsm_state_fetch;
                    end case;
                when others =>
                    r_CurrState <= chip8_fsm_state_fetch;
            end case;
        end if;
    end process;

    process(r_CurrState) is
    begin
        case r_CurrState is
            when chip8_fsm_state_fetch =>
                o_PCWrite <= '0';
                o_IRWrite <= '1';
                o_RRWrite <= '0';
                o_RegFileWrite <= '0';
                o_ALUOp <= chip8_alu_add;
            when chip8_fsm_state_decode =>
                o_PCWrite <= '0';
                o_IRWrite <= '0';
                o_RRWrite <= '1';
                o_RegFileWrite <= '0';
                o_ALUOp <= chip8_alu_add;
            when others =>
                o_PCWrite <= '0';
                o_IRWrite <= '0';
                o_RRWrite <= '0';
                o_RegFileWrite <= '1';
                o_ALUOp <= chip8_alu_add;
        end case;
    end process;

end architecture;
